// Logisim project ALU.circ as structural Verilog: 1 circuit, main circuit main
module main (
  input  [31:0] a,
  input  [31:0] b,
  input  done,
  input  [3:0] aluop,
  input  output_inverted,
  input  output_inc,
  input  clk,
  input  rst,
  output [31:0] res_low,
  output [31:0] res_high
);

  wire [63:0] adder_1_out, and_1_out, bit_extender_1_out, bit_extender_2_out, or_1_out, subtractor_1_out,
       xor_1_out;

  assign bit_extender_1_out = {{32{a[31]}}, a};  // Bit_Extender bit_extender_1
  assign bit_extender_2_out = {{32{b[31]}}, b};  // Bit_Extender bit_extender_2
  Adder #(.width(64)) adder_1 (.a(bit_extender_1_out), .b(bit_extender_2_out), .out(adder_1_out));  // open: cin, cout
  Subtractor #(.width(64)) subtractor_1 (
    .a(bit_extender_1_out), .b(bit_extender_2_out), .out(subtractor_1_out));  // open: bin, bout
  assign and_1_out = bit_extender_1_out & bit_extender_2_out;  // AND_Gate and_1, 64 bits wide
  assign or_1_out = bit_extender_1_out | bit_extender_2_out;  // OR_Gate or_1, 64 bits wide
  assign xor_1_out = bit_extender_1_out ^ bit_extender_2_out;  // XOR_Gate xor_1, 64 bits wide
  Multiplexer #(.select(4), .width(64)) multiplexer_1 (
    .in0(adder_1_out), .in1(subtractor_1_out), .in4(and_1_out), .in5(or_1_out), .in6(xor_1_out),
    .in7(xor_1_out), .out({res_high, res_low}), .sel(aluop));  // open: in2, in3, in8, in9, in10, in11, in12, in13, in14, in15
endmodule
